// Logisim project 4bit_processor.circ as structural Verilog
module main (
);

  wire A_BT, B_BT, CPU_1_clock, CPU_1_read, CPU_1_write, CPU_ATT, CPU_READY, IO_ACK, IO_ATT, IO_READY, IO_W,
       memory_driver_2_save, RAM_ACK, RAM_ATT, RAM_READY, RAM_W, RESET_out, ROM_ACK, ROM_ATT, ROM_READY,
       SAVE, VRA_W, VRAM_ATT, VRAM_READY;
  wire [1:0] JX, JY;
  wire [2:0] DP_DATA;
  wire [3:0] A0, A1, B0, B1, C0, C1, CPU_1_data_out, D0, D1, io_driver_1_data_out, memory_driver_2_mem_data,
       pull_resistor_1_node, ram_1_dout, rom_1_data, VOL;
  wire [4:0] X_COORD, Y_COORD;
  wire [11:0] CPU_1_address_out, memory_driver_1_mem_address, memory_driver_2_mem_address;
  wire [13:0] FREC;

  Button RESET (.out(RESET_out));
  ROM #(.addrWidth(12), .dataWidth(4)) rom_1 (.addr(memory_driver_1_mem_address), .data(rom_1_data));
  MEMORY_DRIVER memory_driver_1 (
    .ADDRESS_BUS(CPU_1_address_out), .DATA_BUS(pull_resistor_1_node), .ATT(ROM_ATT),
    .MEM_ADDRESS(memory_driver_1_mem_address), .ACK(ROM_ACK));  // open: WRITE, MEM_DATA, SAVE
  Pull_Resistor pull_resistor_1 (.node(pull_resistor_1_node));
  // RGB_Video #(.cursor("No Cursor"), .height(32), .reset("Synchronous"), .scale(8), .width(32)) rgb_video_1: pin names not known; wires that end beside it: SAVE, X_COORD, Y_COORD, DP_DATA
  CPU CPU_1 (
    .DATA_IN(pull_resistor_1_node), .RESET(RESET_out), .ATT(CPU_ATT), .DATA_OUT(CPU_1_data_out),
    .ADDRESS_OUT(CPU_1_address_out), .WRITE(CPU_1_write), .READ(CPU_1_read), .CLOCK(CPU_1_clock));
  assign pull_resistor_1_node = ROM_READY ? rom_1_data : 4'bz;  // Controlled_Buffer controlled_buffer_1
  assign pull_resistor_1_node = CPU_READY ? CPU_1_data_out : 4'bz;  // Controlled_Buffer controlled_buffer_2
  MEMORY_DRIVER memory_driver_2 (
    .ADDRESS_BUS(CPU_1_address_out), .DATA_BUS(pull_resistor_1_node), .ATT(RAM_ATT), .WRITE(RAM_W),
    .MEM_ADDRESS(memory_driver_2_mem_address), .MEM_DATA(memory_driver_2_mem_data),
    .SAVE(memory_driver_2_save), .ACK(RAM_ACK));
  RAM #(.addrWidth(9), .dataWidth(4), .enables("line")) ram_1 (
    .addr(memory_driver_2_mem_address[8:0]), .we(memory_driver_2_save), .clk(memory_driver_2_save),
    .din(memory_driver_2_mem_data), .dout(ram_1_dout));
  _7_Segment_Display u_7_segment_display_1 (
    .g(A0[3]), .f(A0[2]), .a(A0[1]), .b(A0[0]), .e(A1[3]), .d(A1[2]), .c(A1[1]), .dp(A1[0]));
  _7_Segment_Display u_7_segment_display_2 (
    .g(B0[3]), .f(B0[2]), .a(B0[1]), .b(B0[0]), .e(B1[3]), .d(B1[2]), .c(B1[1]), .dp(B1[0]));
  Joystick #(.bits(2)) joystick_1 (.x(JX), .y(JY));
  _7_Segment_Display u_7_segment_display_3 (
    .g(C0[3]), .f(C0[2]), .a(C0[1]), .b(C0[0]), .e(C1[3]), .d(C1[2]), .c(C1[1]), .dp(C1[0]));
  _7_Segment_Display u_7_segment_display_4 (
    .g(D0[3]), .f(D0[2]), .a(D0[1]), .b(D0[0]), .e(D1[3]), .d(D1[2]), .c(D1[1]), .dp(D1[0]));
  Button button_1 (.out(A_BT));
  Button button_2 (.out(B_BT));
  assign pull_resistor_1_node = RAM_READY ? ram_1_dout : 4'bz;  // Controlled_Buffer controlled_buffer_3
  BUS_DRIVER bus_driver_1 (
    .ADDRESS_BUS(CPU_1_address_out), .ROM_ACK(ROM_ACK), .RAM_ACK(RAM_ACK), .IO_ACK(IO_ACK),
    .WRITE(CPU_1_write), .READ(CPU_1_read), .CLOCK(CPU_1_clock), .ROM_ATT(ROM_ATT), .RAM_ATT(RAM_ATT),
    .VRAM_ATT(VRAM_ATT), .IO_ATT(IO_ATT), .CPU_ATT(CPU_ATT), .RAM_W(RAM_W), .VRAM_W(VRA_W), .IO_W(IO_W),
    .CPU_READY(CPU_READY), .ROM_READY(ROM_READY), .RAM_READY(RAM_READY), .VRAM_READY(VRAM_READY),
    .IO_READY(IO_READY));  // open: VRAM_ACK
  DISPLAY_DRIVER display_driver_1 (
    .ADDRESS(CPU_1_address_out), .DATA(pull_resistor_1_node), .ATT(VRAM_ATT), .X_COORD(X_COORD),
    .Y_COORD(Y_COORD), .DATA_OUT(DP_DATA), .SAVE(SAVE));
  // Buzzer #(.vol_width(4)) buzzer_1: pin names not known; wires that end beside it: 1'b1, FREC, VOL
  assign pull_resistor_1_node = IO_READY ? io_driver_1_data_out : 4'bz;  // Controlled_Buffer controlled_buffer_4
  IO_DRIVER io_driver_1 (
    .ADDRESS(CPU_1_address_out), .DATA(pull_resistor_1_node), .ATT(IO_ATT), .WRITE(IO_W), .JX(JX), .JY(JY),
    .A_BT(A_BT), .B_BT(B_BT), .DATA_OUT(io_driver_1_data_out), .ACK(IO_ACK), .A0(A0), .A1(A1), .B0(B0),
    .B1(B1), .C0(C0), .C1(C1), .D0(D0), .D1(D1), .FREC(FREC), .VOL_LVL(VOL));
endmodule

module CPU (
  input  [3:0] DATA_IN,
  input  RESET,
  input  ATT,
  output [3:0] DATA_OUT,
  output [11:0] ADDRESS_OUT,
  output WRITE,
  output READ,
  output CLOCK
);

  wire and_1_out, and_2_out, buffer_7_out, buffer_8_out, InstDecoder_1_address_w, InstDecoder_1_alu_out,
       InstDecoder_1_carry_out, InstDecoder_1_carry_r, InstDecoder_1_carry_reset, InstDecoder_1_carry_w,
       InstDecoder_1_data_w, InstDecoder_1_datareg_r, InstDecoder_1_datareg_w, InstDecoder_1_ds_r,
       InstDecoder_1_ds_w, InstDecoder_1_pc_r, InstDecoder_1_pc_up, InstDecoder_1_pc_w,
       InstDecoder_1_pointer_r, InstDecoder_1_pointer_up, InstDecoder_1_pointer_upd, InstDecoder_1_pointer_w,
       InstDecoder_1_register_datain, InstDecoder_1_registerblock_out, InstDecoder_1_result_out,
       InstDecoder_1_set_a, InstDecoder_1_set_b, InstDecoder_1_stack_r, InstDecoder_1_stack_w,
       InstDecoder_1_subs, InstDecoder_1_swap_r, InstDecoder_1_swap_w, InstDecoder_1_zero_out,
       InstDecoder_1_zero_r, InstDecoder_1_zero_reset, InstDecoder_1_zero_w, not_1_out, not_2_out, not_3_out,
       or_1_out, pull_resistor_3_node;
  wire [3:0] ALU_1_data_out, buffer_1_out, buffer_2_out, buffer_3_out, buffer_4_out, buffer_5_out,
       buffer_6_out, pull_resistor_2_node, RegisterBlock_1_dataout;

  Pull_Resistor pull_resistor_1 (.node(DATA_IN));
  Pull_Resistor pull_resistor_2 (.node(pull_resistor_2_node));
  assign pull_resistor_2_node = pull_resistor_3_node ? DATA_IN : 4'bz;  // Controlled_Buffer controlled_buffer_1
  Pull_Resistor pull_resistor_3 (.node(pull_resistor_3_node));
  InstDecoder InstDecoder_1 (
    .DATA(pull_resistor_2_node), .RESET(RESET), .ATT(ATT), .DATA_IN(pull_resistor_3_node),
    .SET_A(InstDecoder_1_set_a), .SET_B(InstDecoder_1_set_b), .RESULT_OUT(InstDecoder_1_result_out),
    .CARRY_OUT(InstDecoder_1_carry_out), .ZERO_OUT(InstDecoder_1_zero_out), .SUBS(InstDecoder_1_subs),
    .PC_R(InstDecoder_1_pc_r), .PC_W(InstDecoder_1_pc_w), .PC_UP(InstDecoder_1_pc_up),
    .POINTER_R(InstDecoder_1_pointer_r), .POINTER_W(InstDecoder_1_pointer_w),
    .POINTER_UP(InstDecoder_1_pointer_up), .STACK_W(InstDecoder_1_stack_w), .STACK_R(InstDecoder_1_stack_r),
    .DATAREG_W(InstDecoder_1_datareg_w), .DATAREG_R(InstDecoder_1_datareg_r),
    .REGISTER_DATAIN(InstDecoder_1_register_datain), .POINTER_UPD(InstDecoder_1_pointer_upd),
    .CARRY_W(InstDecoder_1_carry_w), .ZERO_W(InstDecoder_1_zero_w), .ZERO_R(InstDecoder_1_zero_r),
    .CARRY_R(InstDecoder_1_carry_r), .CARRY_RESET(InstDecoder_1_carry_reset),
    .ZERO_RESET(InstDecoder_1_zero_reset), .DS_R(InstDecoder_1_ds_r), .DATA_W(InstDecoder_1_data_w),
    .ADDRESS_W(InstDecoder_1_address_w), .ALU_OUT(InstDecoder_1_alu_out),
    .REGISTERBLOCK_OUT(InstDecoder_1_registerblock_out), .SWAP_W(InstDecoder_1_swap_w),
    .SWAP_R(InstDecoder_1_swap_r), .WRITE(WRITE), .READ(READ), .CLOCK_OUT(CLOCK), .DS_W(InstDecoder_1_ds_w));
  assign pull_resistor_2_node = InstDecoder_1_alu_out ? ALU_1_data_out : 4'bz;  // Controlled_Buffer controlled_buffer_2
  ALU ALU_1 (
    .DataIn(pull_resistor_2_node), .RESULT_OUT(InstDecoder_1_result_out), .SET_A(InstDecoder_1_set_a),
    .CARRY_OUT(InstDecoder_1_carry_out), .ZERO_OUT(InstDecoder_1_zero_out), .SET_B(InstDecoder_1_set_b),
    .SUBS(InstDecoder_1_subs), .Data_Out(ALU_1_data_out));
  assign pull_resistor_2_node = InstDecoder_1_registerblock_out ? RegisterBlock_1_dataout : 4'bz;  // Controlled_Buffer controlled_buffer_3
  RegisterBlock RegisterBlock_1 (
    .Datain(pull_resistor_2_node), .PC_R(InstDecoder_1_pc_r), .PC_W(InstDecoder_1_pc_w),
    .POINTER_R(InstDecoder_1_pointer_r), .PC_UP(InstDecoder_1_pc_up), .POINTER_W(InstDecoder_1_pointer_w),
    .PointerUP(InstDecoder_1_pointer_up), .STACK_W(InstDecoder_1_stack_w), .STACK_R(InstDecoder_1_stack_r),
    .DATAREG_W(InstDecoder_1_datareg_w), .DATAREG_READ(InstDecoder_1_datareg_r),
    .Datain_EN(InstDecoder_1_register_datain), .POINTER_UPD(InstDecoder_1_pointer_upd),
    .CARRY_W(InstDecoder_1_carry_w), .ZERO_W(InstDecoder_1_zero_w), .ZERO_R(InstDecoder_1_zero_r),
    .CARRY_R(InstDecoder_1_carry_r), .CARRY_RESET(InstDecoder_1_carry_reset),
    .ZERO_RESET(InstDecoder_1_zero_reset), .DS_R(InstDecoder_1_ds_r), .SWAP_W(InstDecoder_1_swap_w),
    .SWAP_R(InstDecoder_1_swap_r), .DS_W(InstDecoder_1_ds_w), .DataOut(RegisterBlock_1_dataout));  // open: PC_CARRY
  Register #(.width(4)) register_1 (
    .D(pull_resistor_2_node), .en(InstDecoder_1_data_w), .clk(InstDecoder_1_data_w), .Q(DATA_OUT),
    .clr(or_1_out));
  assign buffer_1_out = pull_resistor_2_node;  // Buffer buffer_1, 4 bits wide
  assign buffer_2_out = buffer_1_out;  // Buffer buffer_2, 4 bits wide
  assign buffer_3_out = pull_resistor_2_node;  // Buffer buffer_3, 4 bits wide
  assign buffer_4_out = buffer_3_out;  // Buffer buffer_4, 4 bits wide
  assign buffer_5_out = buffer_4_out;  // Buffer buffer_5, 4 bits wide
  assign buffer_6_out = buffer_5_out;  // Buffer buffer_6, 4 bits wide
  Register #(.width(12)) register_2 (
    .D({buffer_6_out, buffer_2_out, pull_resistor_2_node}), .en(InstDecoder_1_address_w),
    .clk(InstDecoder_1_address_w), .Q(ADDRESS_OUT), .clr(or_1_out));
  or or_1 (or_1_out, and_2_out, and_1_out);
  and and_1 (and_1_out, not_1_out, buffer_7_out);
  not not_1 (not_1_out, buffer_7_out);
  buf buffer_7 (buffer_7_out, buffer_8_out);
  buf buffer_8 (buffer_8_out, CLOCK);
  and and_2 (and_2_out, not_2_out, not_3_out);
  not not_2 (not_2_out, not_3_out);
  not not_3 (not_3_out, buffer_7_out);
endmodule

module InstDecoder (
  input  [3:0] DATA,
  input  RESET,
  input  ATT,
  output DATA_IN,
  output SET_A,
  output SET_B,
  output RESULT_OUT,
  output CARRY_OUT,
  output ZERO_OUT,
  output SUBS,
  output PC_R,
  output PC_W,
  output PC_UP,
  output POINTER_R,
  output POINTER_W,
  output POINTER_UP,
  output STACK_W,
  output STACK_R,
  output DATAREG_W,
  output DATAREG_R,
  output REGISTER_DATAIN,
  output POINTER_UPD,
  output CARRY_W,
  output ZERO_W,
  output ZERO_R,
  output CARRY_R,
  output CARRY_RESET,
  output ZERO_RESET,
  output DS_R,
  output DATA_W,
  output ADDRESS_W,
  output ALU_OUT,
  output REGISTERBLOCK_OUT,
  output SWAP_W,
  output SWAP_R,
  output WRITE,
  output READ,
  output CLOCK_OUT,
  output DS_W
);

  wire and_1_out, and_2_out, and_4_out, and_5_out, and_6_out, and_7_out, and_8_out, buffer_1_out,
       buffer_2_out, buffer_3_out, buffer_4_out, buffer_5_out, buffer_6_out, buffer_7_out, buffer_8_out,
       buffer_9_out, buffer_10_out, buffer_11_out, buffer_12_out, buffer_13_out, buffer_14_out,
       buffer_15_out, buffer_16_out, buffer_17_out, buffer_18_out, buffer_19_out, buffer_20_out,
       buffer_21_out, buffer_22_out, buffer_23_out, buffer_24_out, buffer_25_out, buffer_26_out,
       buffer_27_out, buffer_28_out, buffer_29_out, buffer_30_out, buffer_31_out, buffer_32_out,
       buffer_33_out, buffer_34_out, buffer_35_out, buffer_36_out, buffer_37_out, buffer_38_out,
       buffer_39_out, buffer_40_out, buffer_41_out, buffer_42_out, buffer_43_out, buffer_44_out,
       buffer_45_out, buffer_46_out, buffer_47_out, buffer_48_out, buffer_49_out, buffer_50_out,
       buffer_51_out, buffer_52_out, buffer_53_out, buffer_55_out, buffer_56_out, buffer_57_out,
       buffer_58_out, buffer_59_out, buffer_60_out, buffer_61_out, buffer_62_out, buffer_63_out,
       buffer_64_out, buffer_65_out, buffer_66_out, buffer_67_out, buffer_68_out, buffer_69_out,
       buffer_70_out, buffer_71_out, buffer_72_out, buffer_73_out, buffer_74_out, buffer_75_out,
       buffer_76_out, buffer_77_out, buffer_78_out, buffer_79_out, buffer_80_out, buffer_81_out,
       buffer_82_out, buffer_83_out, buffer_84_out, buffer_85_out, buffer_86_out, buffer_87_out,
       buffer_88_out, buffer_89_out, buffer_90_out, buffer_91_out, buffer_92_out, buffer_93_out,
       buffer_94_out, buffer_95_out, buffer_96_out, buffer_97_out, buffer_98_out, buffer_99_out,
       buffer_100_out, buffer_101_out, buffer_102_out, buffer_103_out, buffer_104_out, buffer_105_out,
       buffer_106_out, buffer_107_out, buffer_108_out, buffer_109_out, buffer_110_out, buffer_111_out,
       buffer_112_out, buffer_113_out, buffer_114_out, buffer_115_out, buffer_116_out, buffer_117_out,
       buffer_118_out, buffer_119_out, buffer_120_out, buffer_121_out, buffer_122_out, buffer_123_out,
       buffer_124_out, buffer_125_out, buffer_126_out, buffer_127_out, buffer_128_out, buffer_129_out,
       buffer_130_out, buffer_131_out, buffer_132_out, buffer_133_out, buffer_134_out, buffer_135_out,
       buffer_136_out, buffer_137_out, buffer_138_out, buffer_139_out, buffer_140_out, buffer_141_out,
       buffer_142_out, buffer_143_out, buffer_144_out, buffer_145_out, buffer_146_out, buffer_147_out,
       buffer_148_out, buffer_149_out, buffer_150_out, buffer_151_out, buffer_152_out, buffer_153_out,
       buffer_154_out, buffer_155_out, buffer_156_out, buffer_157_out, buffer_158_out, buffer_159_out,
       buffer_160_out, buffer_161_out, buffer_162_out, buffer_163_out, buffer_164_out, buffer_165_out,
       buffer_166_out, buffer_167_out, buffer_168_out, buffer_169_out, buffer_170_out, buffer_171_out,
       buffer_172_out, buffer_173_out, buffer_174_out, buffer_175_out, buffer_176_out, buffer_177_out,
       buffer_178_out, buffer_179_out, buffer_180_out, buffer_181_out, buffer_182_out, buffer_183_out,
       buffer_184_out, buffer_185_out, buffer_186_out, buffer_187_out, buffer_188_out, buffer_189_out,
       buffer_190_out, buffer_191_out, buffer_192_out, buffer_193_out, buffer_194_out, buffer_195_out,
       buffer_196_out, buffer_197_out, buffer_198_out, buffer_199_out, buffer_200_out, buffer_201_out,
       buffer_202_out, buffer_203_out, buffer_204_out, buffer_205_out, buffer_206_out, buffer_207_out,
       buffer_208_out, buffer_209_out, buffer_210_out, buffer_211_out, buffer_212_out, buffer_213_out,
       buffer_214_out, buffer_215_out, buffer_216_out, buffer_217_out, buffer_218_out, buffer_219_out,
       buffer_220_out, buffer_221_out, buffer_222_out, buffer_223_out, buffer_224_out, buffer_225_out,
       buffer_226_out, buffer_227_out, buffer_228_out, buffer_229_out, buffer_230_out, buffer_231_out,
       buffer_232_out, buffer_233_out, buffer_234_out, buffer_235_out, buffer_236_out, buffer_237_out,
       buffer_238_out, buffer_239_out, buffer_240_out, buffer_241_out, buffer_242_out, buffer_243_out,
       buffer_244_out, buffer_245_out, buffer_246_out, buffer_247_out, buffer_248_out, buffer_249_out,
       buffer_250_out, buffer_251_out, buffer_252_out, buffer_253_out, buffer_254_out, buffer_255_out,
       buffer_256_out, buffer_257_out, buffer_258_out, buffer_259_out, buffer_260_out, buffer_261_out,
       buffer_262_out, buffer_263_out, buffer_264_out, buffer_265_out, buffer_266_out, buffer_267_out,
       buffer_268_out, buffer_269_out, buffer_270_out, buffer_271_out, buffer_272_out, buffer_273_out,
       buffer_274_out, buffer_275_out, buffer_276_out, buffer_277_out, buffer_278_out, buffer_279_out,
       buffer_280_out, buffer_281_out, buffer_282_out, buffer_283_out, buffer_284_out, buffer_285_out,
       buffer_286_out, buffer_287_out, buffer_288_out, buffer_289_out, buffer_290_out, buffer_291_out,
       buffer_292_out, buffer_293_out, buffer_294_out, buffer_295_out, buffer_296_out, buffer_297_out,
       buffer_298_out, buffer_299_out, buffer_300_out, buffer_301_out, buffer_302_out, buffer_303_out,
       buffer_304_out, buffer_305_out, buffer_306_out, buffer_307_out, buffer_308_out, buffer_309_out,
       buffer_310_out, buffer_311_out, buffer_312_out, buffer_313_out, buffer_314_out, buffer_315_out,
       buffer_316_out, buffer_317_out, buffer_318_out, buffer_319_out, buffer_320_out, buffer_321_out,
       buffer_322_out, buffer_323_out, buffer_324_out, delay, demultiplexer_1_out0, demultiplexer_1_out1,
       demultiplexer_1_out2, demultiplexer_1_out3, demultiplexer_1_out4, demultiplexer_1_out5,
       demultiplexer_1_out6, demultiplexer_1_out7, demultiplexer_1_out8, demultiplexer_1_out9,
       demultiplexer_1_out10, demultiplexer_1_out11, demultiplexer_1_out12, demultiplexer_1_out13,
       demultiplexer_1_out14, demultiplexer_1_out15, not_1_out, not_2_out, not_3_out, not_4_out, not_5_out,
       or_1_out, or_2_out, or_9_out, register_2_q, register_3_q, register_4_q;
  wire [3:0] register_1_q;

  not not_1 (not_1_out, CLOCK_OUT);
  buf buffer_1 (buffer_1_out, 1'b1);
  buf buffer_2 (buffer_2_out, buffer_1_out);
  buf buffer_3 (buffer_3_out, buffer_2_out);
  buf buffer_4 (buffer_4_out, buffer_5_out);
  buf buffer_5 (buffer_5_out, buffer_6_out);
  buf buffer_6 (buffer_6_out, buffer_22_out);
  buf buffer_7 (buffer_7_out, buffer_4_out);
  buf buffer_8 (buffer_8_out, buffer_7_out);
  buf buffer_9 (buffer_9_out, buffer_8_out);
  buf buffer_10 (buffer_10_out, buffer_9_out);
  buf buffer_11 (buffer_11_out, buffer_12_out);
  buf buffer_12 (buffer_12_out, buffer_13_out);
  buf buffer_13 (buffer_13_out, buffer_30_out);
  buf buffer_14 (buffer_14_out, buffer_11_out);
  buf buffer_15 (buffer_15_out, buffer_14_out);
  buf buffer_16 (buffer_16_out, buffer_15_out);
  buf buffer_17 (buffer_17_out, buffer_16_out);
  Pull_Resistor pull_resistor_1 (.node(DATA));
  Register #(.width(4)) register_1 (.D(DATA), .en(buffer_55_out), .clk(buffer_55_out), .Q(register_1_q));  // open: clr
  and and_1 (and_1_out, CLOCK_OUT, not_2_out);
  not not_2 (not_2_out, CLOCK_OUT);
  and and_2 (and_2_out, not_1_out, not_3_out);
  not not_3 (not_3_out, not_1_out);
  buf buffer_18 (buffer_18_out, buffer_3_out);
  buf buffer_19 (buffer_19_out, buffer_18_out);
  buf buffer_20 (buffer_20_out, buffer_19_out);
  buf buffer_21 (buffer_21_out, buffer_20_out);
  buf buffer_22 (buffer_22_out, buffer_23_out);
  buf buffer_23 (buffer_23_out, buffer_24_out);
  buf buffer_24 (buffer_24_out, buffer_25_out);
  buf buffer_25 (buffer_25_out, buffer_45_out);
  buf buffer_26 (buffer_26_out, buffer_10_out);
  buf buffer_27 (buffer_27_out, buffer_26_out);
  buf buffer_28 (buffer_28_out, buffer_27_out);
  buf buffer_29 (buffer_29_out, buffer_28_out);
  buf buffer_30 (buffer_30_out, buffer_31_out);
  buf buffer_31 (buffer_31_out, buffer_32_out);
  buf buffer_32 (buffer_32_out, buffer_33_out);
  buf buffer_33 (buffer_33_out, buffer_50_out);
  buf buffer_34 (buffer_34_out, buffer_17_out);
  buf buffer_35 (buffer_35_out, buffer_34_out);
  buf buffer_36 (buffer_36_out, buffer_35_out);
  buf buffer_37 (buffer_37_out, buffer_36_out);
  Demultiplexer #(.enable("true"), .select(4)) demultiplexer_1 (
    .out0(demultiplexer_1_out0), .out1(demultiplexer_1_out1), .out2(demultiplexer_1_out2),
    .out3(demultiplexer_1_out3), .out4(demultiplexer_1_out4), .out5(demultiplexer_1_out5),
    .out6(demultiplexer_1_out6), .out7(demultiplexer_1_out7), .out8(demultiplexer_1_out8),
    .out9(demultiplexer_1_out9), .out10(demultiplexer_1_out10), .out11(demultiplexer_1_out11),
    .out12(demultiplexer_1_out12), .out13(demultiplexer_1_out13), .out14(demultiplexer_1_out14),
    .out15(demultiplexer_1_out15), .in(1'b1), .sel(register_1_q), .en(and_1_out));
  // AND_Gate and_3 has open pins: in0=not_4_out, out=open
  buf buffer_38 (buffer_38_out, and_2_out);
  buf buffer_39 (buffer_39_out, buffer_38_out);
  buf buffer_40 (buffer_40_out, buffer_39_out);
  buf buffer_41 (buffer_41_out, buffer_40_out);
  buf buffer_42 (buffer_42_out, buffer_21_out);
  buf buffer_43 (buffer_43_out, buffer_42_out);
  buf buffer_44 (buffer_44_out, buffer_43_out);
  buf buffer_45 (buffer_45_out, buffer_46_out);
  buf buffer_46 (buffer_46_out, buffer_44_out);
  Pull_Resistor #(.pull(1)) pull_resistor_2 (.node(delay));
  buf buffer_47 (buffer_47_out, buffer_29_out);
  buf buffer_48 (buffer_48_out, buffer_47_out);
  buf buffer_49 (buffer_49_out, buffer_48_out);
  buf buffer_50 (buffer_50_out, buffer_51_out);
  buf buffer_51 (buffer_51_out, buffer_49_out);
  buf buffer_52 (buffer_52_out, buffer_37_out);
  buf buffer_53 (buffer_53_out, buffer_52_out);
  buf buffer_54 (delay, buffer_53_out);
  buf buffer_55 (buffer_55_out, buffer_60_out);
  not not_4 (not_4_out, delay);
  Clock clock_1 (.out(CLOCK_OUT));
  buf buffer_56 (buffer_56_out, buffer_41_out);
  buf buffer_57 (buffer_57_out, buffer_56_out);
  buf buffer_58 (buffer_58_out, buffer_57_out);
  buf buffer_59 (buffer_59_out, buffer_58_out);
  buf buffer_60 (buffer_60_out, buffer_61_out);
  buf buffer_61 (buffer_61_out, buffer_62_out);
  buf buffer_62 (buffer_62_out, and_4_out);
  Register #(.width(1)) register_2 (
    .D(buffer_63_out), .en(buffer_63_out), .clk(buffer_63_out), .Q(register_2_q), .clr(and_4_out));
  buf buffer_63 (buffer_63_out, buffer_59_out);
  and and_4 (and_4_out, register_2_q, ATT);
  buf buffer_64 (buffer_64_out, demultiplexer_1_out15);
  buf buffer_65 (buffer_65_out, buffer_64_out);
  buf buffer_66 (buffer_66_out, buffer_65_out);
  buf buffer_67 (buffer_67_out, buffer_66_out);
  buf buffer_68 (buffer_68_out, buffer_67_out);
  buf buffer_69 (buffer_69_out, buffer_68_out);
  buf buffer_70 (buffer_70_out, buffer_69_out);
  and and_5 (and_5_out, buffer_70_out, DATA[0]);
  buf buffer_71 (buffer_71_out, and_5_out);
  buf buffer_72 (buffer_72_out, demultiplexer_1_out14);
  buf buffer_73 (buffer_73_out, buffer_72_out);
  or or_1 (or_1_out, buffer_71_out, buffer_70_out);
  buf buffer_74 (buffer_74_out, buffer_73_out);
  buf buffer_75 (buffer_75_out, buffer_74_out);
  buf buffer_76 (buffer_76_out, buffer_75_out);
  buf buffer_77 (buffer_77_out, buffer_76_out);
  buf buffer_78 (buffer_78_out, buffer_77_out);
  and and_6 (and_6_out, buffer_78_out, DATA[0]);
  buf buffer_79 (buffer_79_out, and_6_out);
  buf buffer_80 (buffer_80_out, demultiplexer_1_out13);
  or or_2 (or_2_out, buffer_79_out, buffer_78_out);
  buf buffer_81 (buffer_81_out, buffer_80_out);
  buf buffer_82 (buffer_82_out, buffer_81_out);
  buf buffer_83 (buffer_83_out, buffer_82_out);
  buf buffer_84 (buffer_84_out, demultiplexer_1_out12);
  buf buffer_85 (buffer_85_out, buffer_84_out);
  buf buffer_86 (buffer_86_out, buffer_85_out);
  buf buffer_87 (buffer_87_out, buffer_86_out);
  buf buffer_88 (buffer_88_out, buffer_87_out);
  buf buffer_89 (buffer_89_out, buffer_88_out);
  buf buffer_90 (buffer_90_out, buffer_89_out);
  buf buffer_91 (buffer_91_out, buffer_90_out);
  buf buffer_92 (buffer_92_out, buffer_91_out);
  buf buffer_93 (buffer_93_out, buffer_92_out);
  buf buffer_94 (buffer_94_out, demultiplexer_1_out11);
  buf buffer_95 (buffer_95_out, buffer_93_out);
  buf buffer_96 (buffer_96_out, buffer_95_out);
  buf buffer_97 (buffer_97_out, buffer_94_out);
  buf buffer_98 (buffer_98_out, buffer_97_out);
  buf buffer_99 (buffer_99_out, buffer_98_out);
  buf buffer_100 (buffer_100_out, buffer_99_out);
  buf buffer_101 (buffer_101_out, buffer_100_out);
  buf buffer_102 (buffer_102_out, buffer_101_out);
  buf buffer_103 (buffer_103_out, buffer_102_out);
  buf buffer_104 (buffer_104_out, buffer_103_out);
  buf buffer_105 (buffer_105_out, buffer_104_out);
  buf buffer_106 (buffer_106_out, buffer_105_out);
  buf buffer_107 (buffer_107_out, buffer_106_out);
  buf buffer_108 (buffer_108_out, buffer_107_out);
  buf buffer_109 (buffer_109_out, buffer_108_out);
  buf buffer_110 (buffer_110_out, demultiplexer_1_out10);
  buf buffer_111 (buffer_111_out, buffer_110_out);
  buf buffer_112 (buffer_112_out, buffer_111_out);
  buf buffer_113 (buffer_113_out, buffer_112_out);
  buf buffer_114 (buffer_114_out, buffer_113_out);
  buf buffer_115 (buffer_115_out, buffer_114_out);
  buf buffer_116 (buffer_116_out, buffer_115_out);
  buf buffer_117 (buffer_117_out, buffer_116_out);
  buf buffer_118 (buffer_118_out, buffer_117_out);
  buf buffer_119 (buffer_119_out, buffer_118_out);
  buf buffer_120 (buffer_120_out, buffer_119_out);
  buf buffer_121 (buffer_121_out, buffer_120_out);
  buf buffer_122 (buffer_122_out, buffer_121_out);
  buf buffer_123 (buffer_123_out, buffer_122_out);
  buf buffer_124 (buffer_124_out, buffer_123_out);
  buf buffer_125 (buffer_125_out, buffer_124_out);
  buf buffer_126 (buffer_126_out, buffer_125_out);
  buf buffer_127 (buffer_127_out, buffer_126_out);
  buf buffer_128 (buffer_128_out, buffer_127_out);
  buf buffer_129 (buffer_129_out, buffer_128_out);
  buf buffer_130 (buffer_130_out, buffer_129_out);
  buf buffer_131 (buffer_131_out, buffer_130_out);
  buf buffer_132 (buffer_132_out, buffer_131_out);
  buf buffer_133 (buffer_133_out, buffer_132_out);
  buf buffer_134 (buffer_134_out, buffer_133_out);
  buf buffer_135 (buffer_135_out, buffer_134_out);
  buf buffer_136 (buffer_136_out, buffer_135_out);
  buf buffer_137 (buffer_137_out, buffer_136_out);
  buf buffer_138 (buffer_138_out, buffer_137_out);
  buf buffer_139 (buffer_139_out, buffer_138_out);
  buf buffer_140 (buffer_140_out, buffer_139_out);
  buf buffer_141 (buffer_141_out, buffer_140_out);
  buf buffer_142 (buffer_142_out, buffer_141_out);
  buf buffer_143 (buffer_143_out, buffer_142_out);
  buf buffer_144 (buffer_144_out, buffer_143_out);
  buf buffer_145 (buffer_145_out, buffer_144_out);
  buf buffer_146 (buffer_146_out, buffer_145_out);
  buf buffer_147 (buffer_147_out, buffer_146_out);
  buf buffer_148 (buffer_148_out, buffer_147_out);
  buf buffer_149 (buffer_149_out, buffer_148_out);
  buf buffer_150 (buffer_150_out, buffer_149_out);
  buf buffer_151 (buffer_151_out, buffer_150_out);
  buf buffer_152 (buffer_152_out, demultiplexer_1_out9);
  buf buffer_153 (buffer_153_out, buffer_152_out);
  buf buffer_154 (buffer_154_out, buffer_151_out);
  buf buffer_155 (buffer_155_out, buffer_153_out);
  buf buffer_156 (buffer_156_out, buffer_155_out);
  buf buffer_157 (buffer_157_out, buffer_156_out);
  buf buffer_158 (buffer_158_out, buffer_157_out);
  buf buffer_159 (buffer_159_out, buffer_158_out);
  buf buffer_160 (buffer_160_out, buffer_159_out);
  buf buffer_161 (buffer_161_out, buffer_160_out);
  buf buffer_162 (buffer_162_out, buffer_161_out);
  buf buffer_163 (buffer_163_out, buffer_162_out);
  buf buffer_164 (buffer_164_out, buffer_163_out);
  buf buffer_165 (buffer_165_out, buffer_164_out);
  buf buffer_166 (buffer_166_out, buffer_165_out);
  buf buffer_167 (buffer_167_out, buffer_166_out);
  buf buffer_168 (buffer_168_out, buffer_167_out);
  buf buffer_169 (buffer_169_out, buffer_168_out);
  buf buffer_170 (buffer_170_out, buffer_169_out);
  buf buffer_171 (buffer_171_out, buffer_170_out);
  buf buffer_172 (buffer_172_out, buffer_171_out);
  buf buffer_173 (buffer_173_out, buffer_172_out);
  buf buffer_174 (buffer_174_out, buffer_173_out);
  buf buffer_175 (buffer_175_out, buffer_174_out);
  buf buffer_176 (buffer_176_out, buffer_175_out);
  buf buffer_177 (buffer_177_out, buffer_176_out);
  buf buffer_178 (buffer_178_out, buffer_177_out);
  buf buffer_179 (buffer_179_out, buffer_178_out);
  buf buffer_180 (buffer_180_out, buffer_179_out);
  buf buffer_181 (buffer_181_out, buffer_180_out);
  buf buffer_182 (buffer_182_out, buffer_181_out);
  buf buffer_183 (buffer_183_out, buffer_182_out);
  buf buffer_184 (buffer_184_out, buffer_183_out);
  buf buffer_185 (buffer_185_out, buffer_184_out);
  buf buffer_186 (buffer_186_out, buffer_185_out);
  buf buffer_187 (buffer_187_out, buffer_186_out);
  buf buffer_188 (buffer_188_out, buffer_187_out);
  buf buffer_189 (buffer_189_out, buffer_188_out);
  buf buffer_190 (buffer_190_out, buffer_189_out);
  buf buffer_191 (buffer_191_out, buffer_190_out);
  buf buffer_192 (buffer_192_out, buffer_191_out);
  buf buffer_193 (buffer_193_out, buffer_192_out);
  buf buffer_194 (buffer_194_out, buffer_193_out);
  buf buffer_195 (buffer_195_out, demultiplexer_1_out8);
  buf buffer_196 (buffer_196_out, buffer_195_out);
  buf buffer_197 (buffer_197_out, buffer_196_out);
  buf buffer_198 (buffer_198_out, buffer_194_out);
  buf buffer_199 (buffer_199_out, buffer_197_out);
  buf buffer_200 (buffer_200_out, buffer_199_out);
  buf buffer_201 (buffer_201_out, buffer_200_out);
  buf buffer_202 (buffer_202_out, buffer_201_out);
  buf buffer_203 (buffer_203_out, buffer_202_out);
  buf buffer_204 (buffer_204_out, buffer_203_out);
  buf buffer_205 (buffer_205_out, buffer_204_out);
  buf buffer_206 (buffer_206_out, buffer_205_out);
  buf buffer_207 (buffer_207_out, buffer_206_out);
  buf buffer_208 (buffer_208_out, buffer_207_out);
  buf buffer_209 (buffer_209_out, buffer_208_out);
  buf buffer_210 (buffer_210_out, buffer_209_out);
  buf buffer_211 (buffer_211_out, buffer_210_out);
  buf buffer_212 (buffer_212_out, buffer_211_out);
  buf buffer_213 (buffer_213_out, buffer_212_out);
  buf buffer_214 (buffer_214_out, buffer_213_out);
  buf buffer_215 (buffer_215_out, buffer_214_out);
  buf buffer_216 (buffer_216_out, buffer_215_out);
  buf buffer_217 (buffer_217_out, buffer_216_out);
  buf buffer_218 (buffer_218_out, buffer_217_out);
  buf buffer_219 (buffer_219_out, buffer_218_out);
  buf buffer_220 (buffer_220_out, buffer_219_out);
  buf buffer_221 (buffer_221_out, buffer_220_out);
  buf buffer_222 (buffer_222_out, buffer_221_out);
  buf buffer_223 (buffer_223_out, buffer_222_out);
  buf buffer_224 (buffer_224_out, buffer_223_out);
  buf buffer_225 (buffer_225_out, buffer_224_out);
  buf buffer_226 (buffer_226_out, demultiplexer_1_out6);
  buf buffer_227 (buffer_227_out, buffer_226_out);
  buf buffer_228 (buffer_228_out, buffer_227_out);
  buf buffer_229 (buffer_229_out, demultiplexer_1_out7);
  buf buffer_230 (buffer_230_out, buffer_228_out);
  buf buffer_231 (buffer_231_out, buffer_230_out);
  buf buffer_232 (buffer_232_out, buffer_231_out);
  buf buffer_233 (buffer_233_out, buffer_232_out);
  buf buffer_234 (buffer_234_out, buffer_233_out);
  buf buffer_235 (buffer_235_out, buffer_234_out);
  buf buffer_236 (buffer_236_out, buffer_235_out);
  buf buffer_237 (buffer_237_out, buffer_236_out);
  buf buffer_238 (buffer_238_out, demultiplexer_1_out5);
  buf buffer_239 (buffer_239_out, buffer_237_out);
  buf buffer_240 (buffer_240_out, buffer_239_out);
  buf buffer_241 (buffer_241_out, buffer_238_out);
  buf buffer_242 (buffer_242_out, buffer_241_out);
  buf buffer_243 (buffer_243_out, buffer_242_out);
  buf buffer_244 (buffer_244_out, buffer_243_out);
  buf buffer_245 (buffer_245_out, buffer_244_out);
  buf buffer_246 (buffer_246_out, buffer_245_out);
  buf buffer_247 (buffer_247_out, buffer_246_out);
  buf buffer_248 (buffer_248_out, buffer_247_out);
  buf buffer_249 (buffer_249_out, buffer_248_out);
  buf buffer_250 (buffer_250_out, buffer_249_out);
  buf buffer_251 (buffer_251_out, buffer_250_out);
  buf buffer_252 (buffer_252_out, buffer_251_out);
  buf buffer_253 (buffer_253_out, demultiplexer_1_out4);
  buf buffer_254 (buffer_254_out, buffer_253_out);
  buf buffer_255 (buffer_255_out, buffer_254_out);
  buf buffer_256 (buffer_256_out, buffer_255_out);
  buf buffer_257 (buffer_257_out, buffer_256_out);
  buf buffer_258 (buffer_258_out, buffer_257_out);
  buf buffer_259 (buffer_259_out, buffer_258_out);
  buf buffer_260 (buffer_260_out, buffer_259_out);
  buf buffer_261 (buffer_261_out, demultiplexer_1_out3);
  buf buffer_262 (buffer_262_out, buffer_260_out);
  buf buffer_263 (buffer_263_out, buffer_262_out);
  buf buffer_264 (buffer_264_out, buffer_261_out);
  buf buffer_265 (buffer_265_out, buffer_264_out);
  buf buffer_266 (buffer_266_out, buffer_265_out);
  buf buffer_267 (buffer_267_out, buffer_266_out);
  buf buffer_268 (buffer_268_out, buffer_267_out);
  buf buffer_269 (buffer_269_out, buffer_268_out);
  buf buffer_270 (buffer_270_out, buffer_269_out);
  buf buffer_271 (buffer_271_out, buffer_270_out);
  buf buffer_272 (buffer_272_out, buffer_271_out);
  buf buffer_273 (buffer_273_out, buffer_272_out);
  buf buffer_274 (buffer_274_out, buffer_273_out);
  buf buffer_275 (buffer_275_out, buffer_274_out);
  buf buffer_276 (buffer_276_out, buffer_275_out);
  buf buffer_277 (buffer_277_out, buffer_276_out);
  buf buffer_278 (buffer_278_out, buffer_277_out);
  buf buffer_279 (buffer_279_out, buffer_278_out);
  buf buffer_280 (buffer_280_out, buffer_279_out);
  buf buffer_281 (buffer_281_out, buffer_280_out);
  buf buffer_282 (buffer_282_out, buffer_281_out);
  buf buffer_283 (buffer_283_out, buffer_282_out);
  Register #(.width(1)) register_3 (
    .D(buffer_286_out), .en(buffer_286_out), .clk(buffer_286_out), .Q(register_3_q), .clr(and_7_out));
  buf buffer_284 (buffer_284_out, buffer_283_out);
  buf buffer_285 (buffer_285_out, buffer_284_out);
  buf buffer_286 (buffer_286_out, buffer_285_out);
  and and_7 (and_7_out, ATT, register_3_q);
  buf buffer_287 (buffer_287_out, and_7_out);
  buf buffer_288 (buffer_288_out, buffer_287_out);
  buf buffer_289 (buffer_289_out, demultiplexer_1_out2);
  buf buffer_290 (buffer_290_out, buffer_289_out);
  buf buffer_291 (buffer_291_out, buffer_290_out);
  buf buffer_292 (buffer_292_out, buffer_291_out);
  buf buffer_293 (buffer_293_out, buffer_292_out);
  buf buffer_294 (buffer_294_out, buffer_293_out);
  buf buffer_295 (buffer_295_out, buffer_294_out);
  buf buffer_296 (buffer_296_out, buffer_295_out);
  buf buffer_297 (buffer_297_out, buffer_296_out);
  buf buffer_298 (buffer_298_out, buffer_297_out);
  buf buffer_299 (buffer_299_out, buffer_298_out);
  buf buffer_300 (buffer_300_out, buffer_299_out);
  buf buffer_301 (buffer_301_out, buffer_300_out);
  buf buffer_302 (buffer_302_out, buffer_301_out);
  buf buffer_303 (buffer_303_out, buffer_302_out);
  buf buffer_304 (buffer_304_out, buffer_303_out);
  buf buffer_305 (buffer_305_out, demultiplexer_1_out1);
  buf buffer_306 (buffer_306_out, buffer_305_out);
  buf buffer_307 (buffer_307_out, buffer_304_out);
  buf buffer_308 (buffer_308_out, buffer_306_out);
  buf buffer_309 (buffer_309_out, buffer_308_out);
  buf buffer_310 (buffer_310_out, buffer_309_out);
  buf buffer_311 (buffer_311_out, buffer_310_out);
  buf buffer_312 (buffer_312_out, buffer_311_out);
  buf buffer_313 (buffer_313_out, buffer_312_out);
  buf buffer_314 (buffer_314_out, buffer_313_out);
  buf buffer_315 (buffer_315_out, buffer_314_out);
  buf buffer_316 (buffer_316_out, buffer_315_out);
  buf buffer_317 (buffer_317_out, buffer_316_out);
  buf buffer_318 (buffer_318_out, buffer_317_out);
  buf buffer_319 (buffer_319_out, buffer_318_out);
  buf buffer_320 (buffer_320_out, buffer_319_out);
  buf buffer_321 (buffer_321_out, buffer_320_out);
  Register #(.width(1)) register_4 (
    .D(buffer_322_out), .en(buffer_322_out), .clk(buffer_322_out), .Q(register_4_q), .clr(and_8_out));
  buf buffer_322 (buffer_322_out, buffer_321_out);
  and and_8 (and_8_out, ATT, register_4_q);
  buf buffer_323 (buffer_323_out, and_8_out);
  buf buffer_324 (buffer_324_out, buffer_323_out);
  or or_3 (DATA_IN, and_8_out, and_7_out, and_4_out);
  or or_4 (SET_A, buffer_157_out, buffer_114_out);
  or or_5 (SET_B, buffer_168_out, buffer_125_out);
  or or_6 (RESULT_OUT, buffer_188_out, buffer_145_out);
  or or_7 (CARRY_OUT, buffer_189_out, buffer_146_out);
  or or_8 (ZERO_OUT, buffer_190_out, buffer_147_out);
  Register #(.width(1)) register_5 (.D(or_9_out), .en(or_9_out), .clk(or_9_out), .Q(SUBS), .clr(not_5_out));
  buf or_9 (or_9_out, buffer_125_out);  // OR_Gate
  or or_10 (PC_R, buffer_271_out, buffer_104_out, and_2_out);
  buf or_11 (PC_W, buffer_83_out);  // OR_Gate
  or or_12 (PC_UP, demultiplexer_1_out0, buffer_324_out, buffer_307_out, buffer_288_out, demultiplexer_1_out3, buffer_263_out, buffer_252_out, buffer_109_out, buffer_240_out, buffer_229_out, buffer_225_out, buffer_198_out, buffer_154_out, buffer_96_out, or_2_out, or_1_out);
  or or_13 (POINTER_R, buffer_260_out, demultiplexer_1_out5, buffer_107_out, demultiplexer_1_out7, buffer_223_out, buffer_216_out, buffer_203_out, demultiplexer_1_out8, buffer_105_out, buffer_103_out, demultiplexer_1_out12, demultiplexer_1_out9, demultiplexer_1_out10);
  // OR_Gate or_14 is placed but not wired
  or or_15 (POINTER_UP, demultiplexer_1_out4, buffer_215_out, buffer_99_out, buffer_97_out, demultiplexer_1_out11);
  or or_16 (STACK_W, buffer_263_out, buffer_225_out, buffer_218_out, buffer_109_out, buffer_107_out, buffer_105_out);
  or or_17 (STACK_R, buffer_251_out, buffer_239_out, buffer_215_out, buffer_207_out, buffer_96_out, buffer_164_out, buffer_121_out);
  or or_18 (DATAREG_W, buffer_324_out, buffer_288_out, buffer_252_out, buffer_240_out, buffer_229_out, buffer_193_out, buffer_150_out);
  or or_19 (DATAREG_R, buffer_289_out, buffer_262_out, demultiplexer_1_out6, buffer_152_out, buffer_110_out);
  or or_20 (REGISTER_DATAIN, buffer_323_out, buffer_287_out, buffer_194_out, buffer_193_out, buffer_192_out, buffer_151_out, buffer_150_out, buffer_149_out);
  or or_21 (POINTER_UPD, demultiplexer_1_out4, demultiplexer_1_out5, buffer_215_out, demultiplexer_1_out8, buffer_99_out, buffer_97_out, demultiplexer_1_out11);
  or or_22 (CARRY_W, buffer_194_out, buffer_151_out);
  or or_23 (ZERO_W, buffer_198_out, buffer_154_out);
  buf or_24 (ZERO_R, demultiplexer_1_out14);  // OR_Gate
  buf or_25 (CARRY_R, demultiplexer_1_out15);  // OR_Gate
  // OR_Gate or_26 is placed but not wired
  // OR_Gate or_27 is placed but not wired
  or or_28 (DS_R, demultiplexer_1_out1, demultiplexer_1_out2, demultiplexer_1_out13);
  buf or_29 (DATA_W, buffer_293_out);  // OR_Gate
  or or_30 (ADDRESS_W, buffer_313_out, buffer_296_out, buffer_279_out, buffer_59_out);
  or or_31 (ALU_OUT, buffer_193_out, buffer_192_out, buffer_191_out, buffer_150_out, buffer_149_out, buffer_148_out);
  or or_32 (REGISTERBLOCK_OUT, buffer_312_out, buffer_310_out, buffer_308_out, buffer_295_out, buffer_293_out, buffer_292_out, buffer_291_out, buffer_278_out, buffer_276_out, buffer_274_out, buffer_167_out, buffer_156_out, buffer_124_out, buffer_113_out, buffer_74_out, buffer_66_out, buffer_58_out, buffer_56_out, buffer_40_out);
  or or_33 (SWAP_W, buffer_216_out, buffer_208_out);
  or or_34 (SWAP_R, buffer_224_out, buffer_217_out);
  buf or_35 (WRITE, buffer_307_out);  // OR_Gate
  or or_36 (READ, buffer_314_out, buffer_281_out, buffer_63_out);
  Pull_Resistor pull_resistor_3 (.node(DATA_IN));
  Pull_Resistor pull_resistor_4 (.node(SET_B));
  Pull_Resistor pull_resistor_5 (.node(RESULT_OUT));
  Pull_Resistor pull_resistor_6 (.node(CARRY_OUT));
  not not_5 (not_5_out, CLOCK_OUT);
  Pull_Resistor pull_resistor_7 (.node(PC_W));
  Pull_Resistor pull_resistor_8 (.node(PC_UP));
  Pull_Resistor pull_resistor_9 (.node(POINTER_R));
  buf or_37 (DS_W, buffer_96_out);  // OR_Gate
  Pull_Resistor pull_resistor_10 (.node(SET_A));
  Pull_Resistor pull_resistor_11 (.node(ZERO_OUT));
  Pull_Resistor pull_resistor_12 (.node(SUBS));
  Pull_Resistor pull_resistor_13 (.node(PC_R));
  Pull_Resistor pull_resistor_14 (.node(POINTER_W));
  Pull_Resistor pull_resistor_15 (.node(POINTER_UP));
  Pull_Resistor pull_resistor_16 (.node(STACK_W));
  Pull_Resistor pull_resistor_17 (.node(STACK_R));
  Pull_Resistor pull_resistor_18 (.node(DATAREG_W));
  Pull_Resistor pull_resistor_19 (.node(DATAREG_R));
  Pull_Resistor pull_resistor_20 (.node(REGISTER_DATAIN));
  Pull_Resistor pull_resistor_21 (.node(POINTER_UPD));
  Pull_Resistor pull_resistor_22 (.node(CARRY_W));
  Pull_Resistor pull_resistor_23 (.node(ZERO_W));
  Pull_Resistor pull_resistor_24 (.node(ZERO_R));
  Pull_Resistor pull_resistor_25 (.node(CARRY_R));
  Pull_Resistor pull_resistor_26 (.node(CARRY_RESET));
  Pull_Resistor pull_resistor_27 (.node(ZERO_RESET));
  Pull_Resistor pull_resistor_28 (.node(DS_R));
  Pull_Resistor pull_resistor_29 (.node(DATA_W));
  Pull_Resistor pull_resistor_30 (.node(ADDRESS_W));
  Pull_Resistor pull_resistor_31 (.node(ALU_OUT));
  Pull_Resistor pull_resistor_32 (.node(REGISTERBLOCK_OUT));
  Pull_Resistor pull_resistor_33 (.node(SWAP_W));
  Pull_Resistor pull_resistor_34 (.node(SWAP_R));
  Pull_Resistor pull_resistor_35 (.node(WRITE));
  Pull_Resistor pull_resistor_36 (.node(READ));
  Pull_Resistor pull_resistor_37 (.node(CLOCK_OUT));
  Pull_Resistor pull_resistor_38 (.node(DS_W));
endmodule

module RegisterBlock (
  input  [3:0] Datain,
  input  PC_R,
  input  PC_W,
  input  POINTER_R,
  input  PC_UP,
  input  POINTER_W,
  input  PointerUP,
  input  STACK_W,
  input  STACK_R,
  input  DATAREG_W,
  input  DATAREG_READ,
  input  Datain_EN,
  input  POINTER_UPD,
  input  CARRY_W,
  input  ZERO_W,
  input  ZERO_R,
  input  CARRY_R,
  input  CARRY_RESET,
  input  ZERO_RESET,
  input  DS_R,
  input  SWAP_W,
  input  SWAP_R,
  input  DS_W,
  output [3:0] DataOut,
  output PC_CARRY
);

  wire and_1_out, and_2_out, and_3_out, buffer_2_out, buffer_3_out, buffer_4_out, buffer_5_out, buffer_6_out,
       CARRY_q, demultiplexer_1_out1, demultiplexer_1_out2, demultiplexer_1_out3, not_1_out, or_1_out, ZERO_q;
  wire [3:0] buffer_1_out, buffer_7_out, buffer_8_out, buffer_9_out, buffer_10_out, buffer_11_out,
       buffer_12_out, buffer_13_out, buffer_15_out, buffer_16_out, buffer_17_out, DATA_V, DS_H_q, DS_L_q,
       DS_M_q, STACK_dout, STACK_POINTER_q, SWAP_q;
  wire [7:0] controlled_buffer_11_out;
  wire [11:0] counter_1_q;

  assign DataOut = Datain_EN ? Datain : 4'bz;  // Controlled_Buffer controlled_buffer_1
  Pull_Resistor pull_resistor_1 (.node(DataOut));
  Register #(.width(4)) DATA (.D(DataOut), .en(DATAREG_W), .clk(DATAREG_W), .Q(DATA_V));  // open: clr
  Register #(.width(1)) CARRY (.D(DataOut[0]), .en(CARRY_W), .clk(CARRY_W), .Q(CARRY_q), .clr(CARRY_RESET));
  assign DataOut = DATAREG_READ ? DATA_V : 4'bz;  // Controlled_Buffer controlled_buffer_2
  assign DataOut[0] = CARRY_R ? CARRY_q : 1'bz;  // Controlled_Buffer controlled_buffer_3
  Register #(.width(1)) ZERO (.D(DataOut[0]), .en(ZERO_W), .clk(ZERO_W), .Q(ZERO_q), .clr(ZERO_RESET));
  Counter #(.max('hf), .ongoal("stay"), .width(4)) STACK_POINTER (
    .load(POINTER_W), .up(PointerUP), .count(1'b1), .clk(POINTER_UPD), .D(DataOut), .Q(STACK_POINTER_q));  // open: clr, carry
  assign DataOut[0] = ZERO_R ? ZERO_q : 1'bz;  // Controlled_Buffer controlled_buffer_4
  Demultiplexer #(.select(2)) demultiplexer_1 (
    .out1(demultiplexer_1_out1), .out2(demultiplexer_1_out2), .out3(demultiplexer_1_out3), .in(1'b1),
    .sel(DATA_V[1:0]));  // open: out0
  assign DataOut = POINTER_R ? STACK_POINTER_q : 4'bz;  // Controlled_Buffer controlled_buffer_5
  RAM #(.addrWidth(4), .dataWidth(4), .enables("line")) STACK (
    .addr(buffer_1_out), .we(STACK_W), .clk(STACK_W), .din(DataOut), .dout(STACK_dout));
  assign buffer_1_out = DataOut;  // Buffer buffer_1, 4 bits wide
  Register #(.width(4)) DS_L (.D(DataOut), .en(and_1_out), .clk(and_1_out), .Q(DS_L_q));  // open: clr
  and and_1 (and_1_out, demultiplexer_1_out1, DS_W);
  Register #(.width(4)) DS_M (.D(DataOut), .en(and_2_out), .clk(and_2_out), .Q(DS_M_q));  // open: clr
  and and_2 (and_2_out, demultiplexer_1_out2, DS_W);
  Register #(.width(4)) DS_H (.D(DataOut), .en(and_3_out), .clk(and_3_out), .Q(DS_H_q));  // open: clr
  and and_3 (and_3_out, demultiplexer_1_out3, DS_W);
  assign DataOut = buffer_2_out ? DS_L_q : 4'bz;  // Controlled_Buffer controlled_buffer_6
  buf buffer_2 (buffer_2_out, buffer_3_out);
  buf buffer_3 (buffer_3_out, buffer_4_out);
  assign DataOut = buffer_4_out ? DS_M_q : 4'bz;  // Controlled_Buffer controlled_buffer_7
  buf buffer_4 (buffer_4_out, buffer_5_out);
  buf buffer_5 (buffer_5_out, DS_R);
  assign DataOut = DS_R ? DS_H_q : 4'bz;  // Controlled_Buffer controlled_buffer_8
  assign DataOut = STACK_R ? STACK_dout : 4'bz;  // Controlled_Buffer controlled_buffer_9
  or or_1 (or_1_out, PC_W, PC_UP);
  Register #(.width(4)) SWAP (.D(DataOut), .en(SWAP_W), .clk(SWAP_W), .Q(SWAP_q));  // open: clr
  Counter #(.max('hdff), .width(12)) counter_1 (
    .load(buffer_6_out), .up(1'b1), .count(not_1_out), .clk(or_1_out),
    .D({buffer_8_out, buffer_7_out, DataOut}), .carry(PC_CARRY), .Q(counter_1_q));  // open: clr
  buf buffer_6 (buffer_6_out, PC_W);
  not not_1 (not_1_out, PC_W);
  assign buffer_7_out = buffer_9_out;  // Buffer buffer_7, 4 bits wide
  assign buffer_8_out = buffer_10_out;  // Buffer buffer_8, 4 bits wide
  assign buffer_9_out = DataOut;  // Buffer buffer_9, 4 bits wide
  assign buffer_10_out = buffer_11_out;  // Buffer buffer_10, 4 bits wide
  assign buffer_11_out = buffer_12_out;  // Buffer buffer_11, 4 bits wide
  assign buffer_12_out = DataOut;  // Buffer buffer_12, 4 bits wide
  assign DataOut = SWAP_R ? SWAP_q : 4'bz;  // Controlled_Buffer controlled_buffer_10
  assign {DataOut, controlled_buffer_11_out} = PC_R ? counter_1_q : 12'bz;  // Controlled_Buffer controlled_buffer_11
  assign buffer_13_out = controlled_buffer_11_out[7:4];  // Buffer buffer_13, 4 bits wide
  assign DataOut = buffer_13_out;  // Buffer buffer_14, 4 bits wide
  assign buffer_15_out = controlled_buffer_11_out[3:0];  // Buffer buffer_15, 4 bits wide
  assign buffer_16_out = buffer_15_out;  // Buffer buffer_16, 4 bits wide
  assign buffer_17_out = buffer_16_out;  // Buffer buffer_17, 4 bits wide
  assign DataOut = buffer_17_out;  // Buffer buffer_18, 4 bits wide
endmodule

module ALU (
  input  [3:0] DataIn,
  input  RESULT_OUT,
  input  SET_A,
  input  CARRY_OUT,
  input  ZERO_OUT,
  input  SET_B,
  input  SUBS,
  output [3:0] Data_Out
);

  wire nor_1_out;
  wire [3:0] A_q, adder_1_out, B_q, subtractor_1_out;
  wire [4:0] multiplexer_1_out;
  wire [4:4] adder_1_cout, subtractor_1_bout;

  Pull_Resistor pull_resistor_1 (.node(DataIn));
  Register #(.width(4)) A (.D(DataIn), .en(SET_A), .clk(SET_A), .Q(A_q));  // open: clr
  Register #(.width(4)) B (.D(DataIn), .en(SET_B), .clk(SET_B), .Q(B_q));  // open: clr
  Adder #(.width(4)) adder_1 (.a(A_q), .b(B_q), .out(adder_1_out), .cout(adder_1_cout[4]));  // open: cin
  Subtractor #(.width(4)) subtractor_1 (
    .a(A_q), .b(B_q), .out(subtractor_1_out), .bout(subtractor_1_bout[4]));  // open: bin
  Multiplexer #(.width(5)) multiplexer_1 (
    .in0({adder_1_cout[4], adder_1_out}), .in1({subtractor_1_bout[4], subtractor_1_out}),
    .out(multiplexer_1_out), .sel(SUBS));
  Pull_Resistor pull_resistor_2 (.node(SUBS));
  assign Data_Out[0] = CARRY_OUT ? multiplexer_1_out[4] : 1'bz;  // Controlled_Buffer controlled_buffer_1
  assign Data_Out = RESULT_OUT ? multiplexer_1_out[3:0] : 4'bz;  // Controlled_Buffer controlled_buffer_2
  nor nor_1 (nor_1_out, multiplexer_1_out[0], multiplexer_1_out[1], multiplexer_1_out[2], multiplexer_1_out[3]);
  assign Data_Out[0] = ZERO_OUT ? nor_1_out : 1'bz;  // Controlled_Buffer controlled_buffer_3
  Pull_Resistor pull_resistor_3 (.node(Data_Out));
endmodule

module BUS_DRIVER (
  input  [11:0] ADDRESS_BUS,
  input  ROM_ACK,
  input  RAM_ACK,
  input  VRAM_ACK,
  input  IO_ACK,
  input  WRITE,
  input  READ,
  input  CLOCK,
  output ROM_ATT,
  output RAM_ATT,
  output VRAM_ATT,
  output IO_ATT,
  output CPU_ATT,
  output RAM_W,
  output VRAM_W,
  output IO_W,
  output CPU_READY,
  output ROM_READY,
  output RAM_READY,
  output VRAM_READY,
  output IO_READY
);

  wire and_1_out, and_2_out, and_3_out, and_4_out, and_5_out, and_6_out, and_7_out, and_12_out, and_13_out,
       and_14_out, and_15_out, and_16_out, and_17_out, and_18_out, and_19_out, and_27_out, buffer_1_out,
       buffer_2_out, buffer_3_out, buffer_4_out, buffer_5_out, buffer_6_out, buffer_7_out, buffer_8_out,
       buffer_9_out, buffer_10_out, buffer_11_out, nand_1_out, not_1_out, not_2_out, not_3_out, not_4_out,
       not_5_out, not_6_out, not_7_out, not_8_out, not_9_out, not_10_out, not_11_out, or_1_out, or_2_out,
       or_3_out, or_4_out, register_2_q;

  not not_1 (not_1_out, CLOCK);
  not not_2 (not_2_out, not_1_out);
  not not_3 (not_3_out, CLOCK);
  Register #(.width(1)) register_1 (.D(WRITE), .en(WRITE), .clk(WRITE), .Q(CPU_READY), .clr(or_1_out));
  or or_1 (or_1_out, or_3_out, and_4_out);
  Register #(.width(1)) register_2 (.D(READ), .en(READ), .clk(READ), .Q(register_2_q), .clr(or_2_out));
  or or_2 (or_2_out, and_3_out, or_3_out);
  and and_1 (and_1_out, not_1_out, not_2_out);
  and and_2 (and_2_out, CLOCK, not_3_out);
  not not_4 (not_4_out, CPU_READY);
  and and_3 (and_3_out, not_4_out, CPU_READY);
  and and_4 (and_4_out, register_2_q, not_5_out);
  not not_5 (not_5_out, register_2_q);
  or or_3 (or_3_out, and_1_out, and_2_out);
  and and_5 (and_5_out, ADDRESS_BUS[11], ADDRESS_BUS[10]);
  and and_6 (and_6_out, ~ADDRESS_BUS[9], ADDRESS_BUS[8], ADDRESS_BUS[7], ADDRESS_BUS[6], ADDRESS_BUS[5], ADDRESS_BUS[4]);  // AND_Gate
  and and_7 (and_7_out, ADDRESS_BUS[11], ADDRESS_BUS[10], ADDRESS_BUS[9]);
  or or_4 (or_4_out, CPU_READY, register_2_q);
  and and_8 (ROM_ATT, ~and_5_out, or_4_out);  // AND_Gate
  and and_9 (RAM_ATT, and_5_out, ~and_6_out, ~and_7_out, or_4_out);  // AND_Gate
  and and_10 (IO_ATT, and_5_out, and_6_out, ~and_7_out, or_4_out);  // AND_Gate
  and and_11 (VRAM_ATT, and_7_out, or_4_out);
  buf buffer_1 (buffer_1_out, 1'b0);
  buf buffer_2 (buffer_2_out, buffer_1_out);
  buf buffer_3 (buffer_3_out, buffer_2_out);
  buf buffer_4 (buffer_4_out, buffer_3_out);
  buf buffer_5 (buffer_5_out, buffer_4_out);
  buf buffer_6 (buffer_6_out, buffer_5_out);
  buf buffer_7 (buffer_7_out, buffer_6_out);
  buf buffer_8 (buffer_8_out, buffer_7_out);
  and and_12 (and_12_out, ROM_ACK, not_6_out);
  not not_6 (not_6_out, ROM_ACK);
  and and_13 (and_13_out, RAM_ACK, not_7_out);
  not not_7 (not_7_out, RAM_ACK);
  and and_14 (and_14_out, VRAM_ACK, not_8_out);
  not not_8 (not_8_out, VRAM_ACK);
  and and_15 (and_15_out, IO_ACK, not_9_out);
  not not_9 (not_9_out, IO_ACK);
  buf buffer_9 (buffer_9_out, buffer_8_out);
  not not_10 (not_10_out, buffer_9_out);
  and and_16 (and_16_out, RAM_ATT, and_13_out);
  and and_17 (and_17_out, VRAM_ATT, and_14_out);
  nand nand_1 (nand_1_out, 1'b0, not_10_out);
  and and_18 (and_18_out, ROM_ATT, and_12_out);
  and and_19 (and_19_out, IO_ATT, and_15_out);
  or or_5 (CPU_ATT, and_18_out, and_16_out, and_17_out, and_19_out);
  not not_11 (not_11_out, CPU_READY);
  and and_20 (ROM_READY, ROM_ATT, nand_1_out, register_2_q);
  and and_21 (RAM_READY, RAM_ATT, nand_1_out, register_2_q);
  and and_22 (VRAM_READY, VRAM_ATT, nand_1_out, register_2_q);
  and and_23 (IO_READY, IO_ATT, nand_1_out, register_2_q);
  and and_24 (RAM_W, RAM_ATT, buffer_10_out);
  and and_25 (VRAM_W, VRAM_ATT, buffer_10_out);
  and and_26 (IO_W, IO_ATT, buffer_10_out);
  buf buffer_10 (buffer_10_out, buffer_11_out);
  buf buffer_11 (buffer_11_out, and_27_out);
  and and_27 (and_27_out, not_11_out, CPU_READY);
endmodule

module DISPLAY_DRIVER (
  input  [11:0] ADDRESS,
  input  [3:0] DATA,
  input  ATT,
  output [4:0] X_COORD,
  output [4:0] Y_COORD,
  output [2:0] DATA_OUT,
  output SAVE
);

  wire buffer_1_out;

  assign {Y_COORD[4], DATA_OUT} = ATT ? DATA : 4'bz;  // Controlled_Buffer controlled_buffer_1
  Pull_Resistor pull_resistor_1 (.node({Y_COORD[3:0], X_COORD}));
  assign {Y_COORD[3:0], X_COORD} = ATT ? ADDRESS[8:0] : 9'bz;  // Controlled_Buffer controlled_buffer_2
  Pull_Resistor pull_resistor_2 (.node({Y_COORD[4], DATA_OUT}));
  buf buffer_1 (buffer_1_out, ATT);
  buf buffer_2 (SAVE, buffer_1_out);
endmodule

module MEMORY_DRIVER (
  input  [11:0] ADDRESS_BUS,
  input  [3:0] DATA_BUS,
  input  ATT,
  input  WRITE,
  output [11:0] MEM_ADDRESS,
  output [3:0] MEM_DATA,
  output SAVE,
  output ACK
);

  wire buffer_1_out, buffer_2_out, buffer_3_out, buffer_4_out, buffer_5_out, buffer_6_out, buffer_7_out,
       buffer_8_out, buffer_9_out, buffer_10_out, buffer_11_out, buffer_12_out, buffer_13_out, buffer_14_out;

  buf buffer_1 (buffer_1_out, ATT);
  buf buffer_2 (buffer_2_out, buffer_1_out);
  buf buffer_3 (buffer_3_out, buffer_2_out);
  buf buffer_4 (buffer_4_out, buffer_3_out);
  buf buffer_5 (buffer_5_out, buffer_4_out);
  buf buffer_6 (buffer_6_out, buffer_5_out);
  buf buffer_7 (buffer_7_out, buffer_6_out);
  buf buffer_8 (buffer_8_out, buffer_7_out);
  buf buffer_9 (buffer_9_out, buffer_8_out);
  assign MEM_ADDRESS = ADDRESS_BUS & {12{ATT}};  // AND_Gate and_1, 12 bits wide
  buf buffer_10 (buffer_10_out, buffer_9_out);
  buf buffer_11 (buffer_11_out, buffer_10_out);
  buf buffer_12 (buffer_12_out, buffer_11_out);
  buf buffer_13 (buffer_13_out, buffer_12_out);
  buf buffer_14 (buffer_14_out, buffer_13_out);
  buf buffer_15 (ACK, buffer_14_out);

  assign MEM_DATA = DATA_BUS;
  assign SAVE = WRITE;
endmodule

module IO_DRIVER (
  input  [11:0] ADDRESS,
  input  [3:0] DATA,
  input  ATT,
  input  WRITE,
  input  [1:0] JX,
  input  [1:0] JY,
  input  A_BT,
  input  B_BT,
  output [3:0] DATA_OUT,
  output ACK,
  output [3:0] A0,
  output [3:0] A1,
  output [3:0] B0,
  output [3:0] B1,
  output [3:0] C0,
  output [3:0] C1,
  output [3:0] D0,
  output [3:0] D1,
  output [13:0] FREC,
  output [3:0] VOL_LVL
);

  wire and_1_out, and_2_out, and_3_out, and_4_out, and_5_out, and_6_out, and_7_out, and_8_out, and_9_out,
       and_10_out, and_11_out, buffer_1_out, buffer_2_out, buffer_3_out, demultiplexer_1_out0,
       demultiplexer_1_out1, demultiplexer_1_out2, demultiplexer_1_out3, demultiplexer_1_out4,
       demultiplexer_1_out5, demultiplexer_1_out6, demultiplexer_1_out7, demultiplexer_1_out8,
       demultiplexer_1_out9, demultiplexer_1_out10, demultiplexer_1_out11, demultiplexer_1_out12,
       demultiplexer_1_out13, demultiplexer_1_out14, demultiplexer_1_out15, or_1_out;

  Demultiplexer #(.enable("true"), .select(4)) demultiplexer_1 (
    .out0(demultiplexer_1_out0), .out1(demultiplexer_1_out1), .out2(demultiplexer_1_out2),
    .out3(demultiplexer_1_out3), .out4(demultiplexer_1_out4), .out5(demultiplexer_1_out5),
    .out6(demultiplexer_1_out6), .out7(demultiplexer_1_out7), .out8(demultiplexer_1_out8),
    .out9(demultiplexer_1_out9), .out10(demultiplexer_1_out10), .out11(demultiplexer_1_out11),
    .out12(demultiplexer_1_out12), .out13(demultiplexer_1_out13), .out14(demultiplexer_1_out14),
    .out15(demultiplexer_1_out15), .in(1'b1), .sel(ADDRESS[3:0]), .en(ATT));
  assign DATA_OUT = demultiplexer_1_out14 ? {3'b000, A_BT} : 4'bz;  // Controlled_Buffer controlled_buffer_1
  Register #(.width(4)) register_1 (
    .D(DATA), .en(and_1_out), .clk(and_1_out), .Q({A1[2:1], A0[0], A0[1]}));  // open: clr
  and and_1 (and_1_out, WRITE, demultiplexer_1_out0);
  and and_2 (and_2_out, WRITE, demultiplexer_1_out1);
  assign DATA_OUT = demultiplexer_1_out13 ? {3'b000, A_BT} : 4'bz;  // Controlled_Buffer controlled_buffer_2
  Register #(.width(4)) register_2 (
    .D(DATA), .en(and_2_out), .clk(and_2_out), .Q({A1[0], A0[3:2], A1[3]}));  // open: clr
  assign DATA_OUT = demultiplexer_1_out12 ? {2'b00, JY} : 4'bz;  // Controlled_Buffer controlled_buffer_3
  Register #(.width(4)) register_3 (
    .D(DATA), .en(and_3_out), .clk(and_3_out), .Q({B1[2:1], B0[0], B0[1]}));  // open: clr
  and and_3 (and_3_out, WRITE, demultiplexer_1_out2);
  or or_1 (or_1_out, demultiplexer_1_out11, demultiplexer_1_out12, demultiplexer_1_out13, demultiplexer_1_out14, demultiplexer_1_out15);
  assign DATA_OUT = demultiplexer_1_out11 ? {2'b00, JX} : 4'bz;  // Controlled_Buffer controlled_buffer_4
  Register #(.width(4)) register_4 (
    .D(DATA), .en(and_4_out), .clk(and_4_out), .Q({B1[0], B0[3:2], B1[3]}));  // open: clr
  and and_4 (and_4_out, WRITE, demultiplexer_1_out3);
  Pull_Resistor pull_resistor_1 (.node(DATA_OUT));
  buf buffer_1 (buffer_1_out, or_1_out);
  buf buffer_2 (buffer_2_out, buffer_1_out);
  buf buffer_3 (buffer_3_out, buffer_2_out);
  buf buffer_4 (ACK, buffer_3_out);
  Register #(.width(4)) register_5 (
    .D(DATA), .en(and_5_out), .clk(and_5_out), .Q({C1[2:1], C0[0], C0[1]}));  // open: clr
  and and_5 (and_5_out, WRITE, demultiplexer_1_out4);
  Register #(.width(4)) register_6 (
    .D(DATA), .en(and_6_out), .clk(and_6_out), .Q({C1[0], C0[3:2], C1[3]}));  // open: clr
  and and_6 (and_6_out, WRITE, demultiplexer_1_out5);
  Register #(.width(4)) register_7 (
    .D(DATA), .en(and_7_out), .clk(and_7_out), .Q({D1[2:1], D0[0], D0[1]}));  // open: clr
  and and_7 (and_7_out, WRITE, demultiplexer_1_out6);
  Register #(.width(4)) register_8 (
    .D(DATA), .en(and_8_out), .clk(and_8_out), .Q({D1[0], D0[3:2], D1[3]}));  // open: clr
  and and_8 (and_8_out, WRITE, demultiplexer_1_out7);
  Register #(.width(4)) LOW_HZ (.D(DATA), .en(and_9_out), .clk(and_9_out), .Q(FREC[6:3]));  // open: clr
  and and_9 (and_9_out, WRITE, demultiplexer_1_out8);
  Register #(.width(4)) HIGH_HZ (.D(DATA), .en(and_10_out), .clk(and_10_out), .Q(FREC[10:7]));  // open: clr
  and and_10 (and_10_out, WRITE, demultiplexer_1_out9);
  Register #(.width(4)) VOL (.D(DATA), .en(and_11_out), .clk(and_11_out), .Q(VOL_LVL));  // open: clr
  and and_11 (and_11_out, WRITE, demultiplexer_1_out10);

  assign {FREC[13:11], FREC[2:0]} = 6'b100000;

  // Other names for the same wires on the sheet: A0_t[3:0] = {A1[2:1], A0[0], A0[1]};
  //   A1_t[3:0] = {A1[0], A0[3:2], A1[3]}; A_BT_t[0] = A_BT; B0_t[3:0] = {B1[2:1], B0[0], B0[1]};
  //   B1_t[3:0] = {B1[0], B0[3:2], B1[3]}; B_BT_t[0] = B_BT; C0_t[3:0] = {C1[2:1], C0[0], C0[1]};
  //   C1_t[3:0] = {C1[0], C0[3:2], C1[3]}; D0_t[3:0] = {D1[2:1], D0[0], D0[1]}; D1_t[3:0] = {D1[0], D0[3:2], D1[3]};
  //   L_HZ[3:0] = FREC[6:3]; H_HZ[3:0] = FREC[10:7]; JX_t[1:0] = JX; JY_t[1:0] = JY; VOL[3:0] = VOL_LVL
endmodule
